// Logisim project PFC_v2.circ as structural Verilog: 1 circuit, main circuit main
module main (
);

  wire clock_1_out;

  Register IF_ID (.clk(clock_1_out));  // open: D, en, Q, clr
  Clock clock_1 (.out(clock_1_out));
  Register ID_EX ();  // open: D, en, clk, Q, clr
  Register EX_MEM ();  // open: D, en, clk, Q, clr
  Register MEM_WB ();  // open: D, en, clk, Q, clr
endmodule
