// Logisim project PFC_mini.circ as structural Verilog: 3 circuits, main circuit main
module main (
  input  Start,
  input  Reset
);

  wire ADDR_A, ADDR_B, ADDR_C, ADDR_D, ADDR_Opnd, ALU_CF, ALU_En, ALU_NF, ALU_OF, ALU_ZF, and_3_out,
       clock_2_out, clock_3_out, clock_4_out, clock_5_out, clock_6_out, clock_7_out, clock_8_out,
       clock_9_out, clock_10_out, clock_11_out, clock_12_out, clock_13_out, d_ff_1_q, decoder_2_out0,
       decoder_2_out1, decoder_2_out2, decoder_2_out3, Execute, Fetch_1, Fetch_2, Idle, Jump_En, MMIO,
       multiplexer_3_out, multiplexer_4_out, multiplexer_5_out, multiplexer_6_out, multiplexer_7_out,
       not_1_out, not_2_out, S_CF, S_NF, S_OF, S_ZF, Set_PC, WR_RAM_edge, xor_1_out;
  wire [1:0] CPU_state;
  wire [3:0] binary_to_bcd_converter_1_p2, binary_to_bcd_converter_1_p3, binary_to_bcd_converter_1_p4;
  wire [7:0] A, Address_bus, ALU_out, B, C, D, Data_bus, In_0, In_1, In_2, In_3, multiplexer_1_out,
       multiplexer_2_out, Opcode, Operand, PC, PC_plus_1, Program_out;
  wire [8:0] bit_extender_1_out;
  wire [23:0] Control_signals;

  Hex_Digit_Display hex_digit_display_1 (.value(A[7:4]));  // open: dp
  Hex_Digit_Display hex_digit_display_2 (.value(A[3:0]));  // open: dp
  Hex_Digit_Display hex_digit_display_3 (.value(C[7:4]));  // open: dp
  Hex_Digit_Display hex_digit_display_4 (.value(C[3:0]));  // open: dp
  Hex_Digit_Display hex_digit_display_5 (.value(PC[7:4]));  // open: dp
  Hex_Digit_Display hex_digit_display_6 (.value(PC[3:0]));  // open: dp
  assign bit_extender_1_out = {{1{1'b0}}, C};  // Bit_Extender bit_extender_1
  Clock clock_1 ();  // open: out
  Hex_Digit_Display hex_digit_display_7 (.value(binary_to_bcd_converter_1_p2));  // open: dp
  // Binary_to_BCD_converter binary_to_bcd_converter_1: pin names not known; wires that end beside it: bit_extender_1_out, binary_to_bcd_converter_1_p2, binary_to_bcd_converter_1_p3, binary_to_bcd_converter_1_p4
  Hex_Digit_Display hex_digit_display_8 (.value(B[7:4]));  // open: dp
  Hex_Digit_Display hex_digit_display_9 (.value(B[3:0]));  // open: dp
  Hex_Digit_Display hex_digit_display_10 (.value(D[7:4]));  // open: dp
  Hex_Digit_Display hex_digit_display_11 (.value(D[3:0]));  // open: dp
  LED led_1 (.in(Idle));
  LED led_2 (.in(Fetch_1));
  LED led_3 (.in(Fetch_2));
  LED led_4 (.in(Execute));
  Hex_Digit_Display hex_digit_display_12 (.value(binary_to_bcd_converter_1_p3));  // open: dp
  Hex_Digit_Display hex_digit_display_13 (.value(binary_to_bcd_converter_1_p4));  // open: dp
  Clock clock_2 (.out(clock_2_out));
  Multiplexer #(.width(8)) multiplexer_1 (.in0(PC_plus_1), .in1(Operand), .out(multiplexer_1_out), .sel(Jump_En));
  or or_1 (Set_PC, Fetch_1, Fetch_2, Jump_En);
  and and_1 (MMIO, Address_bus[2], Address_bus[3], Address_bus[4], Address_bus[5], Address_bus[6], Address_bus[7]);
  D_Flip_Flop d_ff_1 (.D(Control_signals[5]), .clk(clock_2_out), .Q(d_ff_1_q));  // open: Qn, preset, reset
  not not_1 (not_1_out, d_ff_1_q);
  Multiplexer #(.width(8)) multiplexer_2 (.in0(Data_bus), .in1(ALU_out), .out(multiplexer_2_out), .sel(ALU_En));
  Register u_PC (.D(multiplexer_1_out), .en(Set_PC), .clk(clock_3_out), .Q(PC), .clr(Reset));
  Clock clock_3 (.out(clock_3_out));
  and and_2 (WR_RAM_edge, Control_signals[5], not_1_out);
  Register Reg_A (.D(multiplexer_2_out), .en(Control_signals[1]), .clk(clock_4_out), .Q(A), .clr(Reset));
  Clock clock_4 (.out(clock_4_out));
  D_Flip_Flop Flag_ZF (.D(multiplexer_3_out), .clk(clock_5_out), .Q(S_ZF), .reset(Reset));  // open: Qn, preset
  Multiplexer multiplexer_3 (.in0(S_NF), .in1(ALU_ZF), .out(multiplexer_3_out), .sel(ALU_En));
  Clock clock_5 (.out(clock_5_out));
  Adder adder_1 (.a(PC), .b(8'h1), .out(PC_plus_1), .cin(1'b0));  // open: cout
  Control_Unit control_unit_1 (
    .Start(Start), .Program_out(Program_out), .Opcode(Opcode), .Reset(Reset), .CPU_state(CPU_state),
    .Control_signals({Control_signals[23:18], ALU_En, ADDR_Opnd, ADDR_D, ADDR_C, ADDR_B, ADDR_A, Control_signals[11:0]}));
  Clock clock_6 (.out(clock_6_out));
  RAM #(.databus("bidir"), .enables("line"), .trigger("high")) Data_Memory (
    .addr(Address_bus), .we(WR_RAM_edge), .oe(Control_signals[10]), .clk(not_2_out), .data(Data_bus));
  not not_2 (not_2_out, MMIO);
  Register Reg_B (.D(Data_bus), .en(Control_signals[2]), .clk(clock_7_out), .Q(B), .clr(Reset));
  Clock clock_7 (.out(clock_7_out));
  D_Flip_Flop Flag_NF (.D(multiplexer_4_out), .clk(clock_6_out), .Q(S_NF), .reset(Reset));  // open: Qn, preset
  Multiplexer multiplexer_4 (.in0(S_NF), .in1(ALU_NF), .out(multiplexer_4_out), .sel(ALU_En));
  ROM Program_Memory (.addr(PC), .data(Program_out));
  Decoder #(.enable("false"), .select(2)) decoder_1 (
    .out0(Idle), .out1(Fetch_1), .out2(Fetch_2), .out3(Execute), .sel(CPU_state));
  Register Reg_C (.D(Data_bus), .en(Control_signals[3]), .clk(clock_8_out), .Q(C), .clr(Reset));
  Clock clock_8 (.out(clock_8_out));
  D_Flip_Flop Flag_CF (.D(multiplexer_5_out), .clk(clock_9_out), .Q(S_CF), .reset(Reset));  // open: Qn, preset
  Multiplexer multiplexer_5 (.in0(S_CF), .in1(ALU_CF), .out(multiplexer_5_out), .sel(Control_signals[18]));
  Clock clock_9 (.out(clock_9_out));
  Multiplexer #(.select(2)) multiplexer_6 (
    .in0(S_ZF), .in1(S_NF), .in2(S_CF), .in3(S_OF), .out(multiplexer_6_out), .sel(Opcode[3:2]));
  xor xor_1 (xor_1_out, multiplexer_6_out, Opcode[4]);
  Register Reg_D (.D(Data_bus), .en(Control_signals[4]), .clk(clock_10_out), .Q(D), .clr(Reset));
  Clock clock_10 (.out(clock_10_out));
  D_Flip_Flop Flag_OF (.D(multiplexer_7_out), .clk(clock_11_out), .Q(S_OF), .reset(Reset));  // open: Qn, preset
  Multiplexer multiplexer_7 (.in0(S_OF), .in1(ALU_OF), .out(multiplexer_7_out), .sel(Control_signals[19]));
  Clock clock_11 (.out(clock_11_out));
  Decoder #(.select(2)) decoder_2 (
    .out0(decoder_2_out0), .out1(decoder_2_out1), .out2(decoder_2_out2), .out3(decoder_2_out3),
    .sel(Address_bus[1:0]), .en(MMIO));
  or or_2 (Jump_En, Control_signals[20], and_3_out);
  and and_3 (and_3_out, Control_signals[21], xor_1_out);
  Controlled_Buffer #(.width(8)) controlled_buffer_1 (.in(In_0), .en(decoder_2_out0));  // open: out
  Controlled_Buffer #(.width(8)) controlled_buffer_2 (.in(In_1), .en(decoder_2_out1));  // open: out
  Controlled_Buffer #(.width(8)) controlled_buffer_3 (.in(In_2), .en(decoder_2_out2));  // open: out
  Controlled_Buffer #(.width(8)) controlled_buffer_4 (.in(In_3), .en(decoder_2_out3));  // open: out
  Register u_Opcode (.D(Program_out), .en(Fetch_1), .clk(clock_12_out), .Q(Opcode), .clr(Reset));
  Clock clock_12 (.out(clock_12_out));
  Register u_Operand (.D(Program_out), .en(Fetch_2), .clk(clock_13_out), .Q(Operand), .clr(Reset));
  Clock clock_13 (.out(clock_13_out));
  Pull_Resistor pull_resistor_1 (.node(Data_bus));
  assign Data_bus = Control_signals[6] ? A : 8'bz;  // Controlled_Buffer controlled_buffer_5
  assign Data_bus = Control_signals[7] ? B : 8'bz;  // Controlled_Buffer controlled_buffer_6
  assign Data_bus = Control_signals[8] ? C : 8'bz;  // Controlled_Buffer controlled_buffer_7
  assign Data_bus = Control_signals[9] ? D : 8'bz;  // Controlled_Buffer controlled_buffer_8
  assign Data_bus = Control_signals[11] ? Operand : 8'bz;  // Controlled_Buffer controlled_buffer_9
  assign Address_bus = ADDR_A ? A : 8'bz;  // Controlled_Buffer controlled_buffer_10
  assign Address_bus = ADDR_B ? B : 8'bz;  // Controlled_Buffer controlled_buffer_11
  assign Address_bus = ADDR_C ? C : 8'bz;  // Controlled_Buffer controlled_buffer_12
  assign Address_bus = ADDR_D ? D : 8'bz;  // Controlled_Buffer controlled_buffer_13
  assign Address_bus = ADDR_Opnd ? Operand : 8'bz;  // Controlled_Buffer controlled_buffer_14
  ALU alu_1 (
    .Opcode(Opcode), .A(A), .B(Data_bus), .CF_in(S_CF), .Result(ALU_out), .ZF_out(ALU_ZF), .NF_out(ALU_NF),
    .CF_out(ALU_CF), .OF_out(ALU_OF));
  Pull_Resistor pull_resistor_2 (.node(Address_bus));

  // Other names for the same wires on the sheet: WR_A = Control_signals[1]; WR_B = Control_signals[2];
  //   WR_C = Control_signals[3]; WR_D = Control_signals[4]; WR_RAM = Control_signals[5]; RD_A = Control_signals[6];
  //   RD_B = Control_signals[7]; RD_C = Control_signals[8]; RD_D = Control_signals[9]; RD_RAM = Control_signals[10];
  //   RD_Opnd = Control_signals[11]; Control_signals[17:12] = {ALU_En, ADDR_Opnd, ADDR_D, ADDR_C, ADDR_B, ADDR_A};
  //   Set_CF = Control_signals[18]; Set_OF = Control_signals[19]; JMP = Control_signals[20];
  //   JMP_Cond = Control_signals[21]; Halt = Control_signals[22]; Data_Mem[7:0] = Data_bus

  // Notes on the sheet:
  //   contents of Program_Memory (hex, n*v repeats v):
  //   98 50 0 30 1 50 1 70 0 74 1 81 50 1 54 0 29 85 f4 7 10
endmodule

module Control_Unit (
  input  Start,
  input  [7:0] Program_out,
  input  [7:0] Opcode,
  input  Reset,
  output [1:0] CPU_state,
  output [23:0] Control_signals
);

  wire clock_1_out, Execute, Fetch_1, Fetch_2, Idle, Inst_length, not_1_out, not_2_out;
  wire [1:0] CPU_next_state;
  wire [7:0] multiplexer_2_out, uCode_ROM_2_data, uCode_ROM_3_data;
  wire [7:1] uCode_ROM_1_data;
  wire [23:0] bit_extender_1_out;

  not not_1 (not_1_out, Inst_length);
  not not_2 (not_2_out, Control_signals[22]);
  Register #(.width(2)) CPU_state_reg (.D(CPU_next_state), .en(1'b1), .clk(clock_1_out), .Q(CPU_state), .clr(Reset));
  Clock clock_1 (.out(clock_1_out));
  xor xor_1 (CPU_next_state[1], CPU_state[1], CPU_state[0]);
  Multiplexer #(.select(2)) multiplexer_1 (
    .in0(Start), .in1(not_1_out), .in2(1'b1), .in3(not_2_out), .out(CPU_next_state[0]), .sel(CPU_state));
  Decoder #(.enable("false"), .select(2)) decoder_1 (
    .out0(Idle), .out1(Fetch_1), .out2(Fetch_2), .out3(Execute), .sel(CPU_state));
  ROM uCode_ROM_1 (.addr(multiplexer_2_out), .data({uCode_ROM_1_data, Inst_length}));
  Multiplexer #(.width(8)) multiplexer_2 (.in0(Opcode), .in1(Program_out), .out(multiplexer_2_out), .sel(Fetch_1));
  ROM uCode_ROM_2 (.addr(Opcode), .data(uCode_ROM_2_data));
  ROM uCode_ROM_3 (.addr(Opcode), .data(uCode_ROM_3_data));
  assign bit_extender_1_out = {{23{Execute}}, Execute};  // Bit_Extender bit_extender_1
  assign Control_signals = bit_extender_1_out & {uCode_ROM_3_data, uCode_ROM_2_data, uCode_ROM_1_data, Inst_length};  // AND_Gate and_1, 24 bits wide

  // Notes on the sheet:
  //   contents of uCode_ROM_1 (hex, n*v repeats v):
  //   32*0 42 82 2 2 44 84 4 4 48 88 8 8 50 90 10 10 4*3 4*5 4*9 4*11 4*60 4*a0 8*20 4*61 4*a1 8*21 4*2
  //   4*4 4*8 4*10 4*3 4*5 4*9 4*11 42 82 2 2 42 82 2 2 42 82 2 2 42 82 2 2 42 82 2 2 42 82 2 2 42 82 6*2
  //   28*3 4*2 64*1
  //   contents of uCode_ROM_2 (hex, n*v repeats v):
  //   34*0 1 2 0 0 1 2 0 0 1 2 0 0 1 2 16*8 10 20 40 80 10 20 40 80 11 21 41 81 12 22 42 82 8*0 4*1 4*2 14
  //   24 44 84 14 24 44 84 14 24 44 84 14 24 44 84 16*4 0 0 1 2 0 0 1 2 0 0 1 2 0 0 1 2 0 0 1 2 0 0 1 2 0
  //   0 1 2 4*0 28*8
  //   contents of uCode_ROM_3 (hex, n*v repeats v):
  //   16*0 16*40 48*0 16*1 16*0 16*1 16*e 12*2 4*6 16*e 12*2 4*6 32*10 32*20
endmodule

module ALU (
  input  [7:0] Opcode,
  input  [7:0] A,
  input  [7:0] B,
  input  CF_in,
  output [7:0] Result,
  output ZF_out,
  output NF_out,
  output CF_out,
  output OF_out
);

  wire Adder_Cin, Adder_Cout, ALU_ADC, ALU_ADD, ALU_AND, ALU_OR, ALU_ROR, ALU_SBC, ALU_SHR, ALU_SHR_ROR,
       ALU_SUB, ALU_subtract, ALU_XOR, and_1_out, and_6_out, and_7_out, and_8_out, and_9_out, and_10_out,
       and_11_out, not_1_out, not_2_out, not_3_out, not_4_out, not_5_out, not_6_out, or_1_out, ROR_Cin;
  wire [7:0] adder_1_out, and_5_out, bit_extender_1_out, multiplexer_1_out, or_4_out, xor_1_out, xor_2_out;

  Decoder #(.enable("false"), .select(3)) decoder_1 (
    .out0(ALU_ADD), .out1(ALU_SUB), .out2(ALU_ADC), .out3(ALU_SBC), .out4(ALU_AND), .out5(ALU_OR),
    .out6(ALU_XOR), .out7(ALU_SHR_ROR), .sel(Opcode[4:2]));
  or or_1 (or_1_out, ALU_ADC, ALU_SBC);
  and and_1 (and_1_out, or_1_out, CF_in);
  and and_2 (ROR_Cin, CF_in, ALU_ROR);
  or or_2 (ALU_subtract, ALU_SUB, ALU_SBC);
  or or_3 (Adder_Cin, ALU_SUB, and_1_out);
  and and_3 (ALU_SHR, ALU_SHR_ROR, not_1_out);
  not not_1 (not_1_out, Opcode[5]);
  and and_4 (ALU_ROR, ALU_SHR_ROR, Opcode[5]);
  assign bit_extender_1_out = {{7{ALU_subtract}}, ALU_subtract};  // Bit_Extender bit_extender_1
  assign and_5_out = A & B;  // AND_Gate and_5, 8 bits wide
  assign or_4_out = A | B;  // OR_Gate or_4, 8 bits wide
  assign xor_1_out = A ^ B;  // XOR_Gate xor_1, 8 bits wide
  assign xor_2_out = B ^ bit_extender_1_out;  // XOR_Gate xor_2, 8 bits wide
  Adder adder_1 (.a(A), .b(xor_2_out), .out(adder_1_out), .cin(Adder_Cin), .cout(Adder_Cout));
  Multiplexer #(.select(2), .width(8)) multiplexer_1 (
    .in0(and_5_out), .in1(or_4_out), .in2(xor_1_out), .in3({ROR_Cin, A[7:1]}), .out(multiplexer_1_out),
    .sel(Opcode[3:2]));
  Multiplexer #(.width(8)) multiplexer_2 (
    .in0(adder_1_out), .in1(multiplexer_1_out), .out({NF_out, Result[6:0]}), .sel(Opcode[4]));
  not not_2 (not_2_out, A[7]);
  not not_3 (not_3_out, B[7]);
  not not_4 (not_4_out, NF_out);
  and and_6 (and_6_out, A[0], ALU_SHR_ROR);
  and and_7 (and_7_out, Adder_Cout, not_5_out);
  not not_5 (not_5_out, Opcode[4]);
  not not_6 (not_6_out, Opcode[2]);
  and and_8 (and_8_out, not_2_out, not_3_out, NF_out, not_6_out);
  and and_9 (and_9_out, A[7], B[7], not_4_out, not_6_out);
  and and_10 (and_10_out, not_2_out, B[7], NF_out, Opcode[2]);
  and and_11 (and_11_out, A[7], not_3_out, not_4_out, Opcode[2]);
  nor nor_1 (ZF_out, Result[0], Result[1], Result[2], Result[3], Result[4], Result[5], Result[6], NF_out);
  or or_5 (CF_out, and_6_out, and_7_out);
  or or_6 (OF_out, and_8_out, and_9_out, and_10_out, and_11_out);

  assign Result[7] = NF_out;

  // Other names for the same wires on the sheet: ALU_A[7:0] = A; SHR_Cout = A[0]; ALU_B[7:0] = B; ALU_CF = CF_out;
  //   ALU_OF = OF_out; ALU_out[7:0] = {NF_out, Result[6:0]}; ALU_NF = NF_out; ALU_ZF = ZF_out; S_CF = CF_in
endmodule
